// Logisim project 4bitSignedAdder.circ as structural Verilog: 2 circuits, main circuit main
module main (
  input  [3:0] A,
  input  [3:0] B,
  output [3:0] sum,
  output overflow
);

  wire undriven, undriven_2, undriven_3;

  FullAdder bit0 (.Cin(1'b1), .A(A[0]), .B(B[0]), .S(sum[0]), .Cout(undriven));
  FullAdder bit1 (.Cin(undriven), .A(A[1]), .B(B[1]), .S(sum[1]), .Cout(undriven_2));
  FullAdder bit2 (.Cin(undriven_2), .A(A[2]), .B(B[2]), .S(sum[2]), .Cout(undriven_3));
  FullAdder bit3 (.Cin(undriven_3), .A(A[3]), .B(B[3]), .S(sum[3]), .Cout(overflow));
endmodule

module FullAdder (
  input  Cin,
  input  A,
  input  B,
  input  S,
  input  Cout
);

  wire and_1_out, and_2_out, or_1_out, xor_1_out, xor_2_out;

  xor xor_1 (xor_1_out, A, B);
  xor xor_2 (xor_2_out, xor_1_out, Cin);
  and and_1 (and_1_out, Cin, xor_1_out);
  and and_2 (and_2_out, B, A);
  or or_1 (or_1_out, and_1_out, and_2_out);
endmodule
