// Logisim project 4bitSignedAdder.v2.circ as structural Verilog: 1 circuit, main circuit main
module main (
  input  [3:0] A,
  input  [3:0] B,
  output [3:0] sum,
  output overflow
);

  wire and_1_out, and_2_out, and_3_out, and_4_out, and_5_out, and_6_out, and_7_out, and_8_out, or_1_out,
       or_2_out, or_3_out, or_4_out, xor_1_out, xor_2_out, xor_4_out, xor_5_out;

  xor xor_1 (xor_1_out, A[0], B[0]);
  xor xor_2 (xor_2_out, A[1], B[1]);
  xor xor_3 (sum[0], xor_1_out, 1'b0);
  and and_1 (and_1_out, 1'b0, xor_1_out);
  and and_2 (and_2_out, B[0], A[0]);
  xor xor_4 (xor_4_out, A[2], B[2]);
  xor xor_5 (xor_5_out, A[3], B[3]);
  or or_1 (or_1_out, and_1_out, and_2_out);
  xor xor_6 (sum[1], xor_2_out, or_1_out);
  and and_3 (and_3_out, or_1_out, xor_2_out);
  and and_4 (and_4_out, B[1], A[1]);
  xor xor_7 (sum[2], xor_4_out, or_2_out);
  and and_5 (and_5_out, or_2_out, xor_4_out);
  and and_6 (and_6_out, B[2], A[2]);
  xor xor_8 (sum[3], xor_5_out, or_3_out);
  and and_7 (and_7_out, or_3_out, xor_5_out);
  and and_8 (and_8_out, B[3], A[3]);
  or or_2 (or_2_out, and_3_out, and_4_out);
  or or_3 (or_3_out, and_5_out, and_6_out);
  or or_4 (or_4_out, and_7_out, and_8_out);
  xor xor_9 (overflow, or_3_out, or_4_out);
endmodule
