// Logisim project doubleFlipflop.circ as structural Verilog: 1 circuit, main circuit main
module main (
  output D1
);

  wire clock_1_out, Q1_q, Q2_q;

  not not_1 (D1, Q2_q);
  D_Flip_Flop Q1 (.D(D1), .clk(clock_1_out), .Q(Q1_q));  // open: Qn, preset, reset
  Clock clock_1 (.out(clock_1_out));
  D_Flip_Flop Q2 (.D(Q1_q), .clk(clock_1_out), .Q(Q2_q));  // open: Qn, preset, reset
endmodule
