// Logisim project exam2.circ as structural Verilog: 1 circuit, main circuit main
module main (
  output Q0,
  output Q1
);

  wire clock_1_out, d_ff_1_qn, d_ff_2_qn;

  Clock clock_1 (.out(clock_1_out));
  D_Flip_Flop d_ff_1 (.D(d_ff_1_qn), .clk(clock_1_out), .Q(Q0), .Qn(d_ff_1_qn));  // open: preset, reset
  D_Flip_Flop d_ff_2 (.D(d_ff_2_qn), .clk(d_ff_1_qn), .Q(Q1), .Qn(d_ff_2_qn));  // open: preset, reset

  // Notes on the sheet:
  //   Clk
  //   D0
  //   D1
endmodule
